// Logisim project 74LS147.circ as structural Verilog: 2 circuits, main circuit main
module main (
  input  _0,
  input  _1,
  input  _2,
  input  _3,
  input  _4,
  input  _5,
  input  _6,
  input  _7,
  input  _8,
  input  _9
);

  wire n74ls147_1_a, n74ls147_1_b, n74ls147_1_c, n74ls147_1_d;

  _74LS147 u_74ls147_1 (
    .I0(_0), .I1(_1), .I2(_2), .I3(_3), .I4(_4), .I5(_5), .I6(_6), .I7(_7), .I8(_8), .I9(_9),
    .D(n74ls147_1_d), .C(n74ls147_1_c), .B(n74ls147_1_b), .A(n74ls147_1_a));
  LED D (.in(n74ls147_1_d));
  LED C (.in(n74ls147_1_c));
  LED A (.in(n74ls147_1_a));
  LED B (.in(n74ls147_1_b));
endmodule

module _74LS147 (
  input  I0,
  input  I1,
  input  I2,
  input  I3,
  input  I4,
  input  I5,
  input  I6,
  input  I7,
  input  I8,
  input  I9,
  output D,
  output C,
  output B,
  output A
);

  wire and_2_out, and_3_out, and_4_out, and_5_out, and_6_out, and_7_out, not_1_out, not_2_out, not_3_out,
       not_4_out, not_5_out, not_6_out, not_7_out, not_8_out, not_9_out, not_10_out, not_11_out, not_12_out,
       not_13_out, not_14_out, not_15_out, not_16_out, not_17_out, not_18_out, not_19_out, not_20_out,
       not_21_out, not_22_out, not_23_out, not_24_out, not_25_out, not_26_out, not_27_out, not_28_out,
       not_29_out, not_30_out, or_2_out, or_3_out, or_4_out;

  or or_1 (D, I8, I9);
  or or_2 (or_2_out, I4, I5, I6, I7);
  not not_1 (not_1_out, I8);
  not not_2 (not_2_out, I9);
  or or_3 (or_3_out, I2, I3);
  not not_3 (not_3_out, I4);
  not not_4 (not_4_out, I5);
  not not_5 (not_5_out, I6);
  not not_6 (not_6_out, I7);
  not not_7 (not_7_out, I8);
  not not_8 (not_8_out, I9);
  or or_4 (or_4_out, I6, I7);
  not not_9 (not_9_out, I8);
  not not_10 (not_10_out, I9);
  not not_11 (not_11_out, I2);
  not not_12 (not_12_out, I3);
  not not_13 (not_13_out, I4);
  not not_14 (not_14_out, I5);
  not not_15 (not_15_out, I6);
  not not_16 (not_16_out, I7);
  not not_17 (not_17_out, I8);
  not not_18 (not_18_out, I9);
  not not_19 (not_19_out, I4);
  not not_20 (not_20_out, I5);
  not not_21 (not_21_out, I6);
  not not_22 (not_22_out, I7);
  not not_23 (not_23_out, I8);
  not not_24 (not_24_out, I9);
  not not_25 (not_25_out, I6);
  not not_26 (not_26_out, I7);
  not not_27 (not_27_out, I8);
  not not_28 (not_28_out, I9);
  not not_29 (not_29_out, I8);
  not not_30 (not_30_out, I9);
  and and_1 (C, or_2_out, not_1_out, not_2_out);
  and and_2 (and_2_out, or_3_out, not_3_out, not_4_out, not_5_out, not_6_out, not_7_out, not_8_out);
  and and_3 (and_3_out, or_4_out, not_9_out, not_10_out);
  and and_4 (and_4_out, I1, not_11_out, not_12_out, not_13_out, not_14_out, not_15_out, not_16_out, not_17_out, not_18_out);
  and and_5 (and_5_out, I3, not_19_out, not_20_out, not_21_out, not_22_out, not_23_out, not_24_out);
  and and_6 (and_6_out, I5, not_25_out, not_26_out, not_27_out, not_28_out);
  and and_7 (and_7_out, I7, not_29_out, not_30_out);
  or or_5 (B, and_2_out, and_3_out);
  or or_6 (A, and_4_out, and_5_out, and_6_out, and_7_out, I9);
endmodule
