// Logisim project Multiplicador de 4 bits.circ as structural Verilog: 3 circuits, main circuit main
module main (
  input  A0,
  input  A1,
  input  A2,
  input  A3,
  input  B0,
  input  B1,
  input  B2,
  input  B3
);

  wire and_1_out, and_2_out, and_3_out, and_4_out, and_5_out, and_6_out, and_7_out, and_8_out, and_9_out,
       and_10_out, and_11_out, and_12_out, and_13_out, and_14_out, and_15_out, and_16_out,
       meio_somador_1_cout, meio_somador_1_s, meio_somador_2_cout, meio_somador_2_s, meio_somador_3_cout,
       meio_somador_3_s, meio_somador_4_cout, meio_somador_4_s, somador_completo_1_cout,
       somador_completo_1_s, somador_completo_2_cout, somador_completo_2_s, somador_completo_3_cout,
       somador_completo_3_s, somador_completo_4_cout, somador_completo_4_s, somador_completo_5_cout,
       somador_completo_5_s, somador_completo_6_cout, somador_completo_6_s, somador_completo_7_cout,
       somador_completo_7_s, somador_completo_8_cout, somador_completo_8_s;

  and and_1 (and_1_out, A0, B0);
  and and_2 (and_2_out, B0, A1);
  and and_3 (and_3_out, B1, A0);
  and and_4 (and_4_out, B0, A2);
  and and_5 (and_5_out, B1, A1);
  and and_6 (and_6_out, B2, A0);
  and and_7 (and_7_out, B0, A3);
  and and_8 (and_8_out, B1, A2);
  and and_9 (and_9_out, B2, A1);
  and and_10 (and_10_out, B3, A0);
  and and_11 (and_11_out, B1, A3);
  and and_12 (and_12_out, B2, A2);
  and and_13 (and_13_out, B3, A1);
  and and_14 (and_14_out, B2, A3);
  and and_15 (and_15_out, B3, A2);
  and and_16 (and_16_out, B3, A3);
  MEIO_SOMADOR meio_somador_1 (.A(and_2_out), .B(and_3_out), .S(meio_somador_1_s), .Cout(meio_somador_1_cout));
  SOMADOR_COMPLETO somador_completo_1 (
    .A(meio_somador_1_cout), .B(and_4_out), .Cin(and_5_out), .S(somador_completo_1_s),
    .Cout(somador_completo_1_cout));
  SOMADOR_COMPLETO somador_completo_2 (
    .A(somador_completo_1_cout), .B(and_7_out), .Cin(and_8_out), .S(somador_completo_2_s),
    .Cout(somador_completo_2_cout));
  SOMADOR_COMPLETO somador_completo_3 (
    .A(meio_somador_2_cout), .B(and_9_out), .Cin(somador_completo_2_s), .S(somador_completo_3_s),
    .Cout(somador_completo_3_cout));
  SOMADOR_COMPLETO somador_completo_4 (
    .A(somador_completo_2_cout), .B(and_11_out), .Cin(and_12_out), .S(somador_completo_4_s),
    .Cout(somador_completo_4_cout));
  SOMADOR_COMPLETO somador_completo_5 (
    .A(somador_completo_4_cout), .B(and_14_out), .Cin(and_15_out), .S(somador_completo_5_s),
    .Cout(somador_completo_5_cout));
  SOMADOR_COMPLETO somador_completo_6 (
    .A(somador_completo_8_cout), .B(somador_completo_5_cout), .Cin(and_16_out), .S(somador_completo_6_s),
    .Cout(somador_completo_6_cout));
  SOMADOR_COMPLETO somador_completo_7 (
    .A(somador_completo_4_s), .B(somador_completo_3_cout), .Cin(and_13_out), .S(somador_completo_7_s),
    .Cout(somador_completo_7_cout));
  MEIO_SOMADOR meio_somador_2 (
    .A(somador_completo_1_s), .B(and_6_out), .S(meio_somador_2_s), .Cout(meio_somador_2_cout));
  MEIO_SOMADOR meio_somador_3 (
    .A(somador_completo_3_s), .B(and_10_out), .S(meio_somador_3_s), .Cout(meio_somador_3_cout));
  MEIO_SOMADOR meio_somador_4 (
    .A(somador_completo_7_s), .B(meio_somador_3_cout), .S(meio_somador_4_s), .Cout(meio_somador_4_cout));
  SOMADOR_COMPLETO somador_completo_8 (
    .A(meio_somador_4_cout), .B(somador_completo_7_cout), .Cin(somador_completo_5_s),
    .S(somador_completo_8_s), .Cout(somador_completo_8_cout));
  LED led_1 (.in(and_1_out));
  LED led_2 (.in(meio_somador_1_s));
  LED led_3 (.in(meio_somador_2_s));
  LED led_4 (.in(meio_somador_3_s));
  LED led_5 (.in(meio_somador_4_s));
  LED led_6 (.in(somador_completo_8_s));
  LED led_7 (.in(somador_completo_6_s));
  LED led_8 (.in(somador_completo_6_cout));
endmodule

module MEIO_SOMADOR (
  input  A,
  input  B,
  output S,
  output Cout
);

  xor xor_1 (S, A, B);
  and and_1 (Cout, A, B);
endmodule

module SOMADOR_COMPLETO (
  input  A,
  input  B,
  input  Cin,
  output S,
  output Cout
);

  wire and_1_out, and_2_out, and_3_out, xor_1_out;

  xor xor_1 (xor_1_out, A, B);
  and and_1 (and_1_out, B, Cin);
  and and_2 (and_2_out, Cin, A);
  and and_3 (and_3_out, B, A);
  xor xor_2 (S, xor_1_out, Cin);
  or or_1 (Cout, and_1_out, and_2_out, and_3_out);
endmodule
